# Fritzing sketch kosmos_tape_emulator (saved by Fritzing 0.9.3b)
breadboards: 1

parts:
  Part2 = Arduino Leonardo (Rev3b)
  U1 = LCD-16X2 [package=lcd-16x2_noholes]
  S1 = Pushbutton [package="[THT]"]
  S2 = Pushbutton [package="[THT]"]
  S3 = Pushbutton [package="[THT]"]
  S4 = Pushbutton [package="[THT]"]
  R1 = Trimmer Potentiometer [maximum_resistance=10kΩ package=THT]
  R2 = Resistor [tolerance=±5% resistance=220 package=THT]

nets:
  N1: Part2.D2/SDA, U1.RS
  N2: Part2.D3_PWM/SCL, U1.E
  N3: Part2.D4/A6, U1.DB4
  N4: Part2.D5_PWM, U1.DB5
  N5: Part2.D6_PWM/A7, U1.DB6
  N6: Part2.D7, U1.DB7
  5V: Part2.5V, U1.VDD, R1.leg2, R2.Pin_0
  GND: Part2.GND, U1.VSS, U1.R_W, U1.K, S1.Pin_3, S1.Pin_4, S2.Pin_3, S2.Pin_4, S3.Pin_3, S3.Pin_4, S4.Pin_3, S4.Pin_4, R1.leg1
  N7: Part2.A0, S1.Pin_1, S1.Pin_2
  N8: Part2.A1, S3.Pin_1, S3.Pin_2
  N9: Part2.A2, S2.Pin_1, S2.Pin_2
  N10: Part2.A3, S4.Pin_1, S4.Pin_2
  N11: U1.VO, R1.wiper
  N12: U1.A, R2.Pin_1

custom parts:
  Arduino Leonardo (Rev3b): The Arduino Leonardo is a microcontroller board based on the ATmega32u4 (datasheet). It has 20 digital input/output pins (of which 7 can be used as PWM outputs and 12 as analog inputs), a 16 MHz crystal oscillator, a micro USB connection, a power jack, an ICSP header, and a reset button. It contains everything needed to support the microcontroller; simply connect it to a computer with a USB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
